// Logisim project control_logic.circ as structural Verilog: 1 circuit, main circuit control_logic
module control_logic (
  input  [31:0] inst,
  input  BrEq,
  input  BrLt,
  output PCSel,
  output RegWEn,
  output [2:0] ImmSel,
  output BrUn,
  output ASel,
  output BSel,
  output [3:0] ALUSel,
  output MemRW,
  output [1:0] WBSel,
  output CSRSel,
  output CSRWen
);

  wire and_5_out, and_6_out, and_7_out, and_8_out, aupic, comparator_1_eq, comparator_12_eq,
       comparator_14_eq, comparator_15_eq, comparator_16_eq, comparator_17_eq, comparator_18_eq,
       comparator_19_eq, comparator_20_eq, comparator_21_eq, comparator_22_eq, csrw, I, imme, is_mul, is_sra,
       is_sub, jalr, load, lui, not_1_out, not_2_out, or_3_out, or_4_out, or_13_out, R, SB, U, UJ;
  wire [0:0] or_5_out;
  wire [3:0] multiplexer_1_out, multiplexer_2_out, multiplexer_3_out, multiplexer_4_out;

  Comparator #(.mode("unsigned"), .width(7)) comparator_1 (
    .a(7'b0000001), .b(inst[31:25]), .eq(comparator_1_eq));  // open: gt, lt
  Comparator #(.mode("unsigned"), .width(7)) comparator_2 (
    .a(7'b0100000), .b(inst[31:25]), .eq(is_sra));  // open: gt, lt
  Comparator #(.mode("unsigned"), .width(7)) comparator_3 (.a(inst[6:0]), .b(7'b0110011), .eq(R));  // open: gt, lt
  Comparator #(.mode("unsigned"), .width(7)) comparator_4 (.a(inst[6:0]), .b(7'b0000011), .eq(load));  // open: gt, lt
  Comparator #(.mode("unsigned"), .width(7)) comparator_5 (.a(inst[6:0]), .b(7'b0010011), .eq(imme));  // open: gt, lt
  Comparator #(.mode("unsigned"), .width(7)) comparator_6 (.a(inst[6:0]), .b(7'b0100011), .eq(MemRW));  // open: gt, lt
  Comparator #(.mode("unsigned"), .width(7)) comparator_7 (.a(inst[6:0]), .b(7'b1100011), .eq(SB));  // open: gt, lt
  Comparator #(.mode("unsigned"), .width(7)) comparator_8 (.a(inst[6:0]), .b(7'b0010111), .eq(aupic));  // open: gt, lt
  Comparator #(.mode("unsigned"), .width(7)) comparator_9 (.a(inst[6:0]), .b(7'b0110111), .eq(lui));  // open: gt, lt
  Comparator #(.mode("unsigned"), .width(7)) comparator_10 (.a(inst[6:0]), .b(7'b1101111), .eq(UJ));  // open: gt, lt
  Comparator #(.mode("unsigned"), .width(7)) comparator_11 (.a(inst[6:0]), .b(7'b1100111), .eq(jalr));  // open: gt, lt
  Comparator #(.mode("unsigned"), .width(3)) comparator_12 (
    .a(inst[14:12]), .b(3'b001), .eq(comparator_12_eq));  // open: gt, lt
  Comparator #(.mode("unsigned"), .width(7)) comparator_13 (
    .a(inst[6:0]), .b(7'b1110011), .eq(CSRWen));  // open: gt, lt
  Comparator #(.mode("unsigned"), .width(3)) comparator_14 (
    .a(inst[14:12]), .b(3'b101), .eq(comparator_14_eq));  // open: gt, lt
  and and_1 (is_mul, R, comparator_1_eq);
  and and_2 (is_sub, R, is_sra);
  or or_1 (I, load, imme);
  or or_2 (U, aupic, lui);
  and and_3 (csrw, comparator_12_eq, CSRWen);
  and and_4 (CSRSel, CSRWen, comparator_14_eq);
  Multiplexer #(.enable("false"), .select(2), .width(4)) multiplexer_1 (
    .in0(4'b0000), .in1(4'b1010), .in2(4'b1100), .out(multiplexer_1_out), .sel({is_sub, is_mul}));  // open: in3
  Multiplexer #(.enable("false"), .width(4)) multiplexer_2 (
    .in0(4'b0110), .in1(4'b1110), .out(multiplexer_2_out), .sel(is_mul));
  Multiplexer #(.enable("false"), .width(4)) multiplexer_3 (
    .in0(4'b0100), .in1(4'b0101), .out(multiplexer_3_out), .sel(is_sra));
  Comparator #(.mode("unsigned"), .width(3)) comparator_15 (
    .a(inst[14:12]), .b(3'b000), .eq(comparator_15_eq));  // open: gt, lt
  not not_1 (not_1_out, BrEq);
  Comparator #(.mode("unsigned"), .width(3)) comparator_16 (
    .a(inst[14:12]), .b(3'b001), .eq(comparator_16_eq));  // open: gt, lt
  Comparator #(.mode("unsigned"), .width(3)) comparator_17 (
    .a(inst[14:12]), .b(3'b100), .eq(comparator_17_eq));  // open: gt, lt
  Comparator #(.mode("unsigned"), .width(3)) comparator_18 (
    .a(inst[14:12]), .b(3'b110), .eq(comparator_18_eq));  // open: gt, lt
  not not_2 (not_2_out, BrLt);
  Comparator #(.mode("unsigned"), .width(3)) comparator_19 (
    .a(inst[14:12]), .b(3'b101), .eq(comparator_19_eq));  // open: gt, lt
  Comparator #(.mode("unsigned"), .width(3)) comparator_20 (
    .a(inst[14:12]), .b(3'b111), .eq(comparator_20_eq));  // open: gt, lt
  and and_5 (and_5_out, comparator_15_eq, SB, BrEq);
  and and_6 (and_6_out, not_1_out, SB, comparator_16_eq);
  or or_3 (or_3_out, comparator_17_eq, comparator_18_eq);
  or or_4 (or_4_out, comparator_19_eq, comparator_20_eq);
  Multiplexer #(.enable("false"), .select(3), .width(4)) multiplexer_4 (
    .in0(multiplexer_1_out), .in1(multiplexer_2_out), .in2(4'b0111), .in3(4'b1011), .in4(4'b0011),
    .in5(multiplexer_3_out), .in6(4'b0010), .in7(4'b0001), .out(multiplexer_4_out), .sel(inst[14:12]));
  and and_7 (and_7_out, or_3_out, SB, BrLt);
  and and_8 (and_8_out, not_2_out, SB, or_4_out);
  or or_5 (or_5_out[0], R, imme);
  Multiplexer #(.enable("false"), .select(2), .width(4)) multiplexer_5 (
    .in0(4'b0000), .in1(multiplexer_4_out), .in2(4'b1101), .out(ALUSel), .sel({lui, or_5_out[0]}));  // open: in3
  or or_6 (PCSel, and_5_out, and_6_out, and_7_out, and_8_out, UJ, jalr);
  or or_7 (ImmSel[0], MemRW, U, CSRSel);
  or or_8 (ImmSel[1], SB, U);
  or or_9 (ImmSel[2], UJ, CSRSel);
  or or_10 (RegWEn, R, I, U, UJ, jalr);
  or or_11 (WBSel[0], R, imme, U);
  or or_12 (WBSel[1], UJ, jalr);
  Comparator #(.mode("unsigned"), .width(3)) comparator_21 (
    .a(inst[14:12]), .b(3'b110), .eq(comparator_21_eq));  // open: gt, lt
  Comparator #(.mode("unsigned"), .width(3)) comparator_22 (
    .a(inst[14:12]), .b(3'b111), .eq(comparator_22_eq));  // open: gt, lt
  or or_13 (or_13_out, comparator_21_eq, comparator_22_eq);
  or or_14 (ASel, SB, aupic, UJ);
  and and_9 (BrUn, SB, or_13_out);
  or or_15 (BSel, I, MemRW, SB, U, UJ, jalr);

  // Other names for the same wires on the sheet: is_mulh = is_mul; csr = CSRWen; csrwi = CSRSel;
  //   opcode[6:0] = inst[6:0]; funct3[2:0] = inst[14:12]; funct7[6:0] = inst[31:25]; S = MemRW

  // Notes on the sheet:
  //   INPUTS to your circuit
  //   Inst Type
  //   R type and I type -> sra
  //   R type only -> mul, mulh, sub
  //   ALU
  //   DON'T CHANGE THE LOCATIONS OF THE INPUTS AND OUTPUTS!
  //   OUTPUT from your circuit
  //   fuct3=0 -> add, mul, sub
  //   fuct3=1 -> sll, mulh
  //   fuct3=5 -> srl, sra
  //   IF
  //   beq
  //   bne
  //   blt/bltu
  //   bge/bgeu
  //   lui use BSel
  //   R and I use funct3
  //   All others use Add
  //   Decode
  //   ID
  //   MA
  //   WB
  //   bltu
  //   bgeu
  //   CSRW
  //   EX
endmodule
