// Logisim project cpu.circ as structural Verilog: 1 circuit, main circuit cpu
module cpu (
  input  clk,
  input  [31:0] INSTRUCTION,
  input  [31:0] READ_DATA,
  output [31:0] WRITE_ADDRESS,
  output [31:0] PROGRAM_COUNTER,
  output [31:0] ra,
  output [31:0] sp,
  output [31:0] t0,
  output [31:0] t1,
  output [31:0] t2,
  output [31:0] s0,
  output [31:0] s1,
  output [31:0] a0,
  output [31:0] tohost,
  output [3:0] WRITE_ENABLE,
  output [31:0] WRITE_DATA
);

  wire ASel, BrEq, BrLt, BrUn, BSel, CSRSel, CSRWen, MemRW, PCSel, RegWEn;
  wire [1:0] WBSel;
  wire [2:0] funct3, ImmSel;
  wire [3:0] ALUSel, multiplexer_6_out;
  wire [6:0] funct7;
  wire [24:0] INST_ID;
  wire [31:0] adder_1_out, adder_2_out, bit_extender_1_out, bit_extender_2_out, IMME, MEM_DATA,
       multiplexer_1_out, multiplexer_2_out, multiplexer_3_out, multiplexer_4_out, multiplexer_5_out, PC_ID,
       rs1, WRITE_BACK;

  Register #(.width(32)) PC (.D(multiplexer_1_out), .clk(clk), .Q(PROGRAM_COUNTER));  // open: en, clr
  Multiplexer #(.enable("false"), .width(32)) multiplexer_1 (
    .in0(adder_1_out), .in1(WRITE_ADDRESS), .out(multiplexer_1_out), .sel(PCSel));
  Register #(.width(32)) register_1 (
    .D(multiplexer_2_out), .clk(clk), .Q({funct7, INST_ID[24:15], funct3, INST_ID[11:0]}));  // open: en, clr
  Multiplexer #(.enable("false"), .width(32)) multiplexer_2 (
    .in0(INSTRUCTION), .in1(32'h13), .out(multiplexer_2_out), .sel(PCSel));
  Adder #(.width(32)) adder_1 (.a(32'h4), .b(PROGRAM_COUNTER), .out(adder_1_out));  // open: cin, cout
  Register #(.width(32)) register_2 (.D(PROGRAM_COUNTER), .clk(clk), .Q(PC_ID));  // open: en, clr
  control_logic control_logic_1 (
    .CSRWen(CSRWen), .PCSel(PCSel), .RegWEn(RegWEn), .ImmSel(ImmSel), .BrUn(BrUn), .ASel(ASel), .BSel(BSel),
    .ALUSel(ALUSel), .MemRW(MemRW), .WBSel(WBSel), .CSRSel(CSRSel),
    .inst({funct7, INST_ID[24:15], funct3, INST_ID[11:0]}), .BrEq(BrEq), .BrLt(BrLt));
  regfile regfile_1 (
    .rs1(INST_ID[19:15]), .rs2(INST_ID[24:20]), .rd(INST_ID[11:7]), .Write_Data(WRITE_BACK), .RegWEn(RegWEn),
    .clk(clk), .ra(ra), .sp(sp), .t0(t0), .t1(t1), .t2(t2), .s0(s0), .s1(s1), .a0(a0), .Read_Data_1(rs1),
    .Read_Data_2(WRITE_DATA));
  Multiplexer #(.enable("false"), .width(32)) multiplexer_3 (
    .in0(rs1), .in1(PC_ID), .out(multiplexer_3_out), .sel(ASel));
  Multiplexer #(.enable("false"), .width(32)) multiplexer_4 (
    .in0(WRITE_DATA), .in1(IMME), .out(multiplexer_4_out), .sel(BSel));
  alu alu_1 (.Result(WRITE_ADDRESS), .A(multiplexer_3_out), .B(multiplexer_4_out), .ALUSel(ALUSel));
  branch_comp branch_comp_1 (.rs1(rs1), .rs2(WRITE_DATA), .BrUn(BrUn), .BrEq(BrEq), .BrLt(BrLt));
  imm_gen imm_gen_1 (.inst({funct7, INST_ID[24:15], funct3, INST_ID[11:0]}), .ImmSel(ImmSel), .imm(IMME));
  Multiplexer #(.enable("false"), .width(32)) multiplexer_5 (
    .in0(rs1), .in1(IMME), .out(multiplexer_5_out), .sel(CSRSel));
  Multiplexer #(.enable("false"), .select(2), .width(4)) multiplexer_6 (
    .in0(4'b0001), .in1(4'b0011), .in2(4'b1111), .out(multiplexer_6_out), .sel(funct3[1:0]));  // open: in3
  assign bit_extender_1_out = {{24{READ_DATA[7]}}, READ_DATA[7:0]};  // Bit_Extender bit_extender_1
  assign bit_extender_2_out = {{16{READ_DATA[15]}}, READ_DATA[15:0]};  // Bit_Extender bit_extender_2
  Multiplexer #(.enable("false"), .width(4)) multiplexer_7 (
    .in0(4'b0000), .in1(multiplexer_6_out), .out(WRITE_ENABLE), .sel(MemRW));
  Multiplexer #(.enable("false"), .select(2), .width(32)) multiplexer_8 (
    .in0(bit_extender_1_out), .in1(bit_extender_2_out), .in2(READ_DATA), .out(MEM_DATA), .sel(funct3[1:0]));  // open: in3
  csr csr_1 (.CSR_address(12'h51e), .CSR_din(multiplexer_5_out), .CSR_WE(CSRWen), .clk(clk), .tohost(tohost));
  Adder #(.width(32)) adder_2 (.a(PC_ID), .b(32'h4), .out(adder_2_out));  // open: cin, cout
  Multiplexer #(.enable("false"), .select(2), .width(32)) multiplexer_9 (
    .in0(MEM_DATA), .in1(WRITE_ADDRESS), .in2(adder_2_out), .out(WRITE_BACK), .sel(WBSel));  // open: in3

  // Other names for the same wires on the sheet: ALU_OUTPUT[31:0] = WRITE_ADDRESS; opcode[6:0] = INST_ID[6:0];
  //   RW[4:0] = INST_ID[11:7]; INST_ID (some bits) = {funct7, funct3}; RA_t[4:0] = INST_ID[19:15];
  //   RB[4:0] = INST_ID[24:20]; rs2[31:0] = WRITE_DATA

  // Notes on the sheet:
  //   Output to IMEM
  //   IF
  //   IMEM (do **NOT** move this)
  //   Inputs from IMEM
  //   ID
  //   Control
  //   Inputs/Outputs for testing. Do **NOT** move these.
  //   EX
  //   MA
  //   CSR
  //   Outputs To DMEM
  //   DMEM (do **NOT** move this)
  //   Inputs From DMEM
  //   WB
endmodule
